# Fritzing sketch driver-1ch (saved by Fritzing 0.9.2b)
circuit board: 5cm x 5cm
breadboards: 1

parts:
  Q1 = Basic FET N-Channel [package="TO220 [THT]"]
  Q2 = Basic FET P-Channel [package="TO220 [THT]"]
  Q4 = NPN-Transistor [package="TO92 [THT]"]
  R1 = Resistor [tolerance=±5% resistance=4.7k package=THT]
  R2 = Resistor [tolerance=±5% resistance=4.7k package=THT]
  Q5 = NPN-Transistor [package="TO92 [THT]"]
  R3 = Resistor [tolerance=±5% resistance=4.7k package=THT]
  R4 = Resistor [tolerance=±5% resistance=4.7k package=THT]
  JP4 = Header 1 [package=1x01_offset]
  OUT-U = Header 1 [package=1x01_offset]
  JP3 = Header 1 [package=1x01_offset]
  IN-U+ = Header 1 [package=1x01_offset]
  IN-U- = Header 1 [package=1x01_offset]

nets:
  N1: Q1.gate, R2.Pin_1, Q5.C
  N2: Q1.drain, Q2.drain, OUT-U.1
  N3: Q1.source, Q4.E, Q5.E, R3.Pin_1, JP4.1
  N4: Q2.gate, Q4.C, R1.Pin_1
  N5: Q2.source, R1.Pin_0, R2.Pin_0, R4.Pin_0, JP3.1
  N6: Q4.B, R3.Pin_0, IN-U+.1
  N7: Q5.B, R4.Pin_1, IN-U-.1
