# Fritzing sketch driver-3ch-3 (saved by Fritzing 0.9.2b)
circuit board: 5cm x 5cm
breadboards: 1

parts:
  Q1 = Basic FET N-Channel [package="TO220 [THT]"]
  Q4 = NPN-Transistor [package="TO92 [THT]"]
  R1 = Resistor [tolerance=±5% resistance=4.7k package=THT]
  R2 = Resistor [tolerance=±5% resistance=4.7k package=THT]
  Q5 = NPN-Transistor [package="TO92 [THT]"]
  R3 = Resistor [tolerance=±5% resistance=4.7k package=THT]
  R4 = Resistor [tolerance=±5% resistance=4.7k package=THT]
  JP4 = Header 1 [package=1x01_offset]
  OUT-U = Header 1 [package=1x01_offset]
  JP3 = Header 1 [package=1x01_offset]
  IN-U+ = Header 1 [package=1x01_offset]
  IN-U- = Header 1 [package=1x01_offset]
  Q2 = Basic FET P-Channel [package="TO220 [THT]"]
  Q6 = Basic FET N-Channel [package="TO220 [THT]"]
  Q7 = Basic FET P-Channel [package="TO220 [THT]"]
  Q8 = NPN-Transistor [package="TO92 [THT]"]
  Q9 = NPN-Transistor [package="TO92 [THT]"]
  R5 = Resistor [tolerance=±5% resistance=4.7k package=THT]
  R6 = Resistor [tolerance=±5% resistance=4.7k package=THT]
  R7 = Resistor [tolerance=±5% resistance=4.7k package=THT]
  R8 = Resistor [tolerance=±5% resistance=4.7k package=THT]
  JP5 = Header 1 [package=1x01_offset]
  OUT-U1 = Header 1 [package=1x01_offset]
  JP6 = Header 1 [package=1x01_offset]
  IN-U-1 = Header 1 [package=1x01_offset]
  IN-U+1 = Header 1 [package=1x01_offset]
  Q10 = Basic FET N-Channel [package="TO220 [THT]"]
  Q11 = Basic FET P-Channel [package="TO220 [THT]"]
  Q12 = NPN-Transistor [package="TO92 [THT]"]
  Q13 = NPN-Transistor [package="TO92 [THT]"]
  R9 = Resistor [tolerance=±5% resistance=4.7k package=THT]
  R10 = Resistor [tolerance=±5% resistance=4.7k package=THT]
  R11 = Resistor [tolerance=±5% resistance=4.7k package=THT]
  R12 = Resistor [tolerance=±5% resistance=4.7k package=THT]
  JP7 = Header 1 [package=1x01_offset]
  OUT-U2 = Header 1 [package=1x01_offset]
  JP8 = Header 1 [package=1x01_offset]
  IN-U-2 = Header 1 [package=1x01_offset]
  IN-U+2 = Header 1 [package=1x01_offset]

nets:
  N1: Q1.gate, R2.Pin_1, Q5.C
  N2: Q1.drain, OUT-U.1, Q2.drain
  N3: Q1.source, Q4.E, Q5.E, R3.Pin_1, JP4.1
  N4: Q4.B, R3.Pin_0, IN-U+.1
  N5: Q4.C, R1.Pin_1, Q2.gate
  N6: R1.Pin_0, R2.Pin_0, R4.Pin_0, JP3.1, Q2.source
  N7: Q5.B, R4.Pin_1, IN-U-.1
  N8: Q6.gate, Q8.C, R8.Pin_1
  N9: Q6.drain, Q7.drain, OUT-U1.1
  N10: Q6.source, Q8.E, JP5.1
  N11: Q7.gate, Q9.C, R7.Pin_1
  N12: Q7.source, R5.Pin_0, R7.Pin_0, R8.Pin_0, JP6.1
  N13: Q8.B, R5.Pin_1, IN-U-1.1
  N14: Q9.E, R6.Pin_1, Q13.E, R10.Pin_1
  N15: Q9.B, R6.Pin_0, IN-U+1.1
  N16: Q10.gate, Q12.C, R12.Pin_1
  N17: Q10.drain, Q11.drain, OUT-U2.1
  N18: Q10.source, Q12.E, JP7.1
  N19: Q11.gate, Q13.C, R11.Pin_1
  N20: Q11.source, R9.Pin_0, R11.Pin_0, R12.Pin_0, JP8.1
  N21: Q12.B, R9.Pin_1, IN-U-2.1
  N22: Q13.B, R10.Pin_0, IN-U+2.1
