# Fritzing sketch currentsource_mod (saved by Fritzing 0.9.2b)
circuit board: 5cm x 2cm
breadboards: 1

parts:
  I_out- = Header 1 [package=1x01_offset]
  I_out+ = Header 1 [package=1x01_offset]
  V_pwr+ = Header 1 [package=1x01_offset]
  GND_pwr = Header 1 [package=1x01_offset]
  I_set = Header 1 [package=1x01_offset]
  V_ctl = Header 1 [package=1x01_offset]
  GND_ctrl = Header 1 [package=1x01_offset]
  PWM = Header 1 [package=1x01_offset]
  OPAMP1 = Dual Op-Amp [package=so08]
  C1 = Capacitor [package=0805]
  NPNpwm = NPN-Transistor [package="SOT-23 [SMD]"]
  R3 = Resistor [tolerance=±5% resistance=100k package="1206 [SMD]"]
  Rpwm1 = Resistor [tolerance=±5% resistance=1k package="1206 [SMD]"]
  Rmosfet1 = Resistor [tolerance=±5% resistance=100 package="1206 [SMD]"]
  Risetfilter = Resistor [tolerance=±5% resistance=100k package="1206 [SMD]"]
  Rpwm2 = Resistor [tolerance=±5% resistance=100k power=2W package="1206 [SMD]"]
  Rsense = Resistor [tolerance=±5% resistance=0.1 power=2W package="2512 [SMD]"]
  C2 = Capacitor [package=1210]
  Risetfilter1 = Resistor [tolerance=±5% resistance=10k package="1206 [SMD]"]
  Q2 = FET N-Channel, drain tab [part_number=PSMN017-30BL package="D2Pak [SMD]"]

nets:
  N1: I_out-.1, Q2.drain
  N2: I_out+.1, V_pwr+.1
  N3: GND_pwr.1, GND_ctrl.1, OPAMP1.A_V-, C1.2, NPNpwm.2, Rpwm2.Pin_1, Rsense.Pin_1, C2.2
  N4: I_set.1, Risetfilter.Pin_0
  N5: V_ctl.1, OPAMP1.A_V+, C2.1
  N6: PWM.1, Rpwm1.Pin_0, Rpwm2.Pin_0
  N7: OPAMP1.A_OUT, OPAMP1.A_-IN, R3.Pin_0
  N8: OPAMP1.A_+IN, Risetfilter.Pin_1, Risetfilter1.Pin_1
  N9: OPAMP1.B_+IN, NPNpwm.1, R3.Pin_1
  N10: OPAMP1.B_-IN, Rsense.Pin_0, Q2.source
  N11: OPAMP1.B_OUT, Rmosfet1.Pin_0
  N12: C1.1, Risetfilter1.Pin_0
  N13: NPNpwm.0, Rpwm1.Pin_1
  N14: Rmosfet1.Pin_1, Q2.Gate

custom parts:
  FET N-Channel, drain tab: A MOSFET N-Channel Transistor
